// Logisim project computer.circ as structural Verilog
module alu (
  input  [7:0] Data_A,
  input  [7:0] Data_B,
  input  Invert_A,
  input  Invert_B,
  input  Carry_in,
  input  Sub_Op,
  input  Add_Op,
  input  AND_Op,
  input  NAND_Op,
  input  XOR_Op,
  input  OR_OP,
  output [7:0] Result,
  output Carry_out
);

  wire one_bit_alu_2_carry_out, one_bit_alu_3_carry_out, one_bit_alu_4_carry_out, one_bit_alu_5_carry_out,
       one_bit_alu_6_carry_out, one_bit_alu_7_carry_out, one_bit_alu_8_carry_out, or_1_out, or_2_out,
       or_3_out;
  wire [2:0] priority_encoder_1_out;
  wire [7:0] bit_inverter_1_result_a, bit_inverter_1_result_b;

  or or_1 (or_1_out, Invert_B, Sub_Op);
  or or_2 (or_2_out, Carry_in, Sub_Op);
  or or_3 (or_3_out, Sub_Op, Add_Op);
  Priority_Encoder priority_encoder_1 (
    .in0(or_3_out), .in1(AND_Op), .in2(NAND_Op), .in3(XOR_Op), .in4(OR_OP), .out(priority_encoder_1_out));  // open: in5, in6, in7, en_in, gs, en_out
  Bit_inverter bit_inverter_1 (
    .Data_A(Data_A), .Data_B(Data_B), .Invert_A(Invert_A), .Invert_B(or_1_out),
    .Result_A(bit_inverter_1_result_a), .Result_B(bit_inverter_1_result_b));
  one_bit_alu one_bit_alu_1 (
    .A(bit_inverter_1_result_a[7]), .B(bit_inverter_1_result_b[7]), .Carry_in(one_bit_alu_2_carry_out),
    .Operation(priority_encoder_1_out), .Result(Result[7]), .Carry_out(Carry_out));
  one_bit_alu one_bit_alu_2 (
    .A(bit_inverter_1_result_a[6]), .B(bit_inverter_1_result_b[6]), .Carry_in(one_bit_alu_3_carry_out),
    .Operation(priority_encoder_1_out), .Result(Result[6]), .Carry_out(one_bit_alu_2_carry_out));
  one_bit_alu one_bit_alu_3 (
    .A(bit_inverter_1_result_a[5]), .B(bit_inverter_1_result_b[5]), .Carry_in(one_bit_alu_4_carry_out),
    .Operation(priority_encoder_1_out), .Result(Result[5]), .Carry_out(one_bit_alu_3_carry_out));
  one_bit_alu one_bit_alu_4 (
    .A(bit_inverter_1_result_a[4]), .B(bit_inverter_1_result_b[4]), .Carry_in(one_bit_alu_5_carry_out),
    .Operation(priority_encoder_1_out), .Result(Result[4]), .Carry_out(one_bit_alu_4_carry_out));
  one_bit_alu one_bit_alu_5 (
    .A(bit_inverter_1_result_a[3]), .B(bit_inverter_1_result_b[3]), .Carry_in(one_bit_alu_6_carry_out),
    .Operation(priority_encoder_1_out), .Result(Result[3]), .Carry_out(one_bit_alu_5_carry_out));
  one_bit_alu one_bit_alu_6 (
    .A(bit_inverter_1_result_a[2]), .B(bit_inverter_1_result_b[2]), .Carry_in(one_bit_alu_7_carry_out),
    .Operation(priority_encoder_1_out), .Result(Result[2]), .Carry_out(one_bit_alu_6_carry_out));
  one_bit_alu one_bit_alu_7 (
    .A(bit_inverter_1_result_a[1]), .B(bit_inverter_1_result_b[1]), .Carry_in(one_bit_alu_8_carry_out),
    .Operation(priority_encoder_1_out), .Result(Result[1]), .Carry_out(one_bit_alu_7_carry_out));
  one_bit_alu one_bit_alu_8 (
    .A(bit_inverter_1_result_a[0]), .B(bit_inverter_1_result_b[0]), .Carry_in(or_2_out),
    .Operation(priority_encoder_1_out), .Result(Result[0]), .Carry_out(one_bit_alu_8_carry_out));
endmodule

module one_bit_alu (
  input  A,
  input  B,
  input  Carry_in,
  input  [2:0] Operation,
  output Result,
  output Carry_out
);

  wire and_1_out, and_2_out, not_1_out, or_1_out, xor_1_out, xor_2_out;

  xor xor_1 (xor_1_out, A, B);
  or or_1 (or_1_out, A, B);
  xor xor_2 (xor_2_out, xor_1_out, Carry_in);
  and and_1 (and_1_out, xor_1_out, Carry_in);
  and and_2 (and_2_out, A, B);
  or or_2 (Carry_out, and_1_out, and_2_out);
  not not_1 (not_1_out, and_2_out);
  Multiplexer #(.select(3)) multiplexer_1 (
    .in0(xor_2_out), .in1(and_2_out), .in2(not_1_out), .in3(xor_1_out), .in4(or_1_out), .in5(1'b0),
    .in6(1'b0), .in7(1'b0), .out(Result), .sel(Operation));

  // Notes on the sheet:
  //   ADD
  //   AND
  //   NAND
  //   XOR
  //   OR
endmodule

module cpu (
  input  [7:0] Data_In,
  input  Clock,
  input  Reset,
  input  [15:0] Instruction,
  output [7:0] Data_out,
  output [7:0] Address_out,
  output [7:0] Instruction_address
);

  wire and_1_out, dipswitch_1_sw1, instruction_decoder_1_add_op, instruction_decoder_1_and_op,
       instruction_decoder_1_halt, instruction_decoder_1_ldi, instruction_decoder_1_not_op,
       instruction_decoder_1_or_op, instruction_decoder_1_sub_op, instruction_decoder_1_xor_op, not_1_out;
  wire [2:0] instruction_decoder_1_in_reg, instruction_decoder_1_reg_a, instruction_decoder_1_reg_b;
  wire [7:0] alu_1_result, counter_1_q, instruction_decoder_1_data_in, multiplexer_2_out,
       registerfile_1_output_a, registerfile_1_output_b;
  wire [15:0] multiplexer_1_out, rom_1_data;

  ROM #(.dataWidth(16)) rom_1 (.addr(counter_1_q), .data(rom_1_data));
  not not_1 (not_1_out, instruction_decoder_1_halt);
  Multiplexer #(.width(16)) multiplexer_1 (
    .in0(rom_1_data), .in1(Instruction), .out(multiplexer_1_out), .sel(dipswitch_1_sw1));
  and and_1 (and_1_out, Clock, not_1_out);
  DipSwitch dipswitch_1 (.sw1(dipswitch_1_sw1));  // open: sw2, sw3, sw4, sw5, sw6, sw7, sw8
  Counter counter_1 (.clr(Reset), .up(1'b1), .clk(and_1_out), .Q(counter_1_q));  // open: load, count, D, carry
  Instruction_Decoder instruction_decoder_1 (
    .Instruction(multiplexer_1_out), .Reg_A(instruction_decoder_1_reg_a),
    .Reg_B(instruction_decoder_1_reg_b), .In_Reg(instruction_decoder_1_in_reg),
    .Data_In(instruction_decoder_1_data_in), .LDI(instruction_decoder_1_ldi),
    .ADD_Op(instruction_decoder_1_add_op), .SUB_Op(instruction_decoder_1_sub_op),
    .AND_Op(instruction_decoder_1_and_op), .OR_Op(instruction_decoder_1_or_op),
    .XOR_Op(instruction_decoder_1_xor_op), .NOT_Op(instruction_decoder_1_not_op),
    .Halt(instruction_decoder_1_halt));  // open: out_6, out_7, out_8, out_16, out_17, out_18, out_19
  Multiplexer #(.width(8)) multiplexer_2 (
    .in0(alu_1_result), .in1(instruction_decoder_1_data_in), .out(multiplexer_2_out),
    .sel(instruction_decoder_1_ldi));
  RegisterFile registerfile_1 (
    .Clock(and_1_out), .Reset(Reset), .Out_A_Address(instruction_decoder_1_reg_a),
    .Out_B_Address(instruction_decoder_1_reg_b), .Input_Address(instruction_decoder_1_in_reg),
    .Data_In(multiplexer_2_out), .Output_A(registerfile_1_output_a), .Output_B(registerfile_1_output_b));
  // Probe on alu_1_result
  alu alu_1 (
    .Data_A(registerfile_1_output_a), .Data_B(registerfile_1_output_b),
    .Invert_A(instruction_decoder_1_not_op), .Invert_B(1'b0), .Carry_in(1'b0),
    .Sub_Op(instruction_decoder_1_sub_op), .Add_Op(instruction_decoder_1_add_op),
    .AND_Op(instruction_decoder_1_and_op), .NAND_Op(1'b0), .XOR_Op(instruction_decoder_1_xor_op),
    .OR_OP(instruction_decoder_1_or_op), .Result(alu_1_result));  // open: Carry_out

  // Notes on the sheet:
  //   contents of rom_1 (hex, n*v repeats v):
  //   0 42c8 4414 4650 5280 62c0 7440 86c0 9240 f000
endmodule

module RegisterFile (
  input  Clock,
  input  Reset,
  input  [2:0] Out_A_Address,
  input  [2:0] Out_B_Address,
  input  [2:0] Input_Address,
  input  [7:0] Data_In,
  output [7:0] Output_A,
  output [7:0] Output_B
);

  wire decoder_1_out1, decoder_1_out2, decoder_1_out3, decoder_1_out4, decoder_1_out5, decoder_1_out6,
       decoder_1_out7, decoder_2_out0, decoder_2_out1, decoder_2_out2, decoder_2_out3, decoder_2_out4,
       decoder_2_out5, decoder_2_out6, decoder_2_out7, decoder_3_out0, decoder_3_out1, decoder_3_out2,
       decoder_3_out3, decoder_3_out4, decoder_3_out5, decoder_3_out6, decoder_3_out7, not_1_out;
  wire [7:0] register_1_q, register_2_q, register_3_q, register_4_q, register_5_q, register_6_q,
       register_7_q, register_8_q;

  not not_1 (not_1_out, Clock);
  Decoder #(.select(3)) decoder_1 (
    .out1(decoder_1_out1), .out2(decoder_1_out2), .out3(decoder_1_out3), .out4(decoder_1_out4),
    .out5(decoder_1_out5), .out6(decoder_1_out6), .out7(decoder_1_out7), .sel(Input_Address));  // open: out0, en
  Register register_1 (.D(Data_In), .en(1'b0), .clk(not_1_out), .Q(register_1_q), .clr(Reset));
  Register register_2 (.D(Data_In), .en(decoder_1_out1), .clk(not_1_out), .Q(register_2_q), .clr(Reset));
  Register register_3 (.D(Data_In), .en(decoder_1_out2), .clk(not_1_out), .Q(register_3_q), .clr(Reset));
  Register register_4 (.D(Data_In), .en(decoder_1_out3), .clk(not_1_out), .Q(register_4_q), .clr(Reset));
  Register register_5 (.D(Data_In), .en(decoder_1_out4), .clk(not_1_out), .Q(register_5_q), .clr(Reset));
  Register register_6 (.D(Data_In), .en(decoder_1_out5), .clk(not_1_out), .Q(register_6_q), .clr(Reset));
  Register register_7 (.D(Data_In), .en(decoder_1_out6), .clk(not_1_out), .Q(register_7_q), .clr(Reset));
  Register register_8 (.D(Data_In), .en(decoder_1_out7), .clk(not_1_out), .Q(register_8_q));  // open: clr
  assign Output_A = decoder_2_out0 ? register_1_q : 8'bz;  // Controlled_Buffer controlled_buffer_1
  assign Output_B = decoder_3_out0 ? register_1_q : 8'bz;  // Controlled_Buffer controlled_buffer_2
  assign Output_A = decoder_2_out1 ? register_2_q : 8'bz;  // Controlled_Buffer controlled_buffer_3
  assign Output_B = decoder_3_out1 ? register_2_q : 8'bz;  // Controlled_Buffer controlled_buffer_4
  assign Output_A = decoder_2_out2 ? register_3_q : 8'bz;  // Controlled_Buffer controlled_buffer_5
  assign Output_B = decoder_3_out2 ? register_3_q : 8'bz;  // Controlled_Buffer controlled_buffer_6
  assign Output_A = decoder_2_out3 ? register_4_q : 8'bz;  // Controlled_Buffer controlled_buffer_7
  assign Output_B = decoder_3_out3 ? register_4_q : 8'bz;  // Controlled_Buffer controlled_buffer_8
  assign Output_A = decoder_2_out4 ? register_5_q : 8'bz;  // Controlled_Buffer controlled_buffer_9
  assign Output_B = decoder_3_out4 ? register_5_q : 8'bz;  // Controlled_Buffer controlled_buffer_10
  assign Output_A = decoder_2_out5 ? register_6_q : 8'bz;  // Controlled_Buffer controlled_buffer_11
  assign Output_B = decoder_3_out5 ? register_6_q : 8'bz;  // Controlled_Buffer controlled_buffer_12
  assign Output_A = decoder_2_out6 ? register_7_q : 8'bz;  // Controlled_Buffer controlled_buffer_13
  assign Output_B = decoder_3_out6 ? register_7_q : 8'bz;  // Controlled_Buffer controlled_buffer_14
  assign Output_A = decoder_2_out7 ? register_8_q : 8'bz;  // Controlled_Buffer controlled_buffer_15
  assign Output_B = decoder_3_out7 ? register_8_q : 8'bz;  // Controlled_Buffer controlled_buffer_16
  Decoder #(.select(3)) decoder_2 (
    .out0(decoder_2_out0), .out1(decoder_2_out1), .out2(decoder_2_out2), .out3(decoder_2_out3),
    .out4(decoder_2_out4), .out5(decoder_2_out5), .out6(decoder_2_out6), .out7(decoder_2_out7),
    .sel(Out_A_Address));  // open: en
  Decoder #(.select(3)) decoder_3 (
    .out0(decoder_3_out0), .out1(decoder_3_out1), .out2(decoder_3_out2), .out3(decoder_3_out3),
    .out4(decoder_3_out4), .out5(decoder_3_out5), .out6(decoder_3_out6), .out7(decoder_3_out7),
    .sel(Out_B_Address));  // open: en
endmodule

module Bit_inverter (
  input  [7:0] Data_A,
  input  [7:0] Data_B,
  input  Invert_A,
  input  Invert_B,
  output [7:0] Result_A,
  output [7:0] Result_B
);

  wire not_1_out, not_2_out, not_3_out, not_4_out, not_5_out, not_6_out, not_7_out, not_8_out, not_9_out,
       not_10_out, not_11_out, not_12_out, not_13_out, not_14_out, not_15_out, not_16_out;

  not not_1 (not_1_out, Data_B[7]);
  not not_2 (not_2_out, Data_B[6]);
  not not_3 (not_3_out, Data_B[5]);
  not not_4 (not_4_out, Data_B[4]);
  not not_5 (not_5_out, Data_B[3]);
  not not_6 (not_6_out, Data_B[2]);
  not not_7 (not_7_out, Data_B[1]);
  not not_8 (not_8_out, Data_B[0]);
  Multiplexer multiplexer_1 (.in0(Data_A[7]), .in1(not_9_out), .out(Result_A[7]), .sel(Invert_A));
  not not_9 (not_9_out, Data_A[7]);
  Multiplexer multiplexer_2 (.in0(Data_B[7]), .in1(not_1_out), .out(Result_B[7]), .sel(Invert_B));
  Multiplexer multiplexer_3 (.in0(Data_A[6]), .in1(not_10_out), .out(Result_A[6]), .sel(Invert_A));
  not not_10 (not_10_out, Data_A[6]);
  Multiplexer multiplexer_4 (.in0(Data_B[6]), .in1(not_2_out), .out(Result_B[6]), .sel(Invert_B));
  Multiplexer multiplexer_5 (.in0(Data_A[5]), .in1(not_11_out), .out(Result_A[5]), .sel(Invert_A));
  not not_11 (not_11_out, Data_A[5]);
  Multiplexer multiplexer_6 (.in0(Data_B[5]), .in1(not_3_out), .out(Result_B[5]), .sel(Invert_B));
  Multiplexer multiplexer_7 (.in0(Data_A[4]), .in1(not_12_out), .out(Result_A[4]), .sel(Invert_A));
  not not_12 (not_12_out, Data_A[4]);
  Multiplexer multiplexer_8 (.in0(Data_B[4]), .in1(not_4_out), .out(Result_B[4]), .sel(Invert_B));
  Multiplexer multiplexer_9 (.in0(Data_A[3]), .in1(not_13_out), .out(Result_A[3]), .sel(Invert_A));
  not not_13 (not_13_out, Data_A[3]);
  Multiplexer multiplexer_10 (.in0(Data_B[3]), .in1(not_5_out), .out(Result_B[3]), .sel(Invert_B));
  Multiplexer multiplexer_11 (.in0(Data_A[2]), .in1(not_14_out), .out(Result_A[2]), .sel(Invert_A));
  not not_14 (not_14_out, Data_A[2]);
  Multiplexer multiplexer_12 (.in0(Data_B[2]), .in1(not_6_out), .out(Result_B[2]), .sel(Invert_B));
  Multiplexer multiplexer_13 (.in0(Data_A[1]), .in1(not_15_out), .out(Result_A[1]), .sel(Invert_A));
  not not_15 (not_15_out, Data_A[1]);
  Multiplexer multiplexer_14 (.in0(Data_B[1]), .in1(not_7_out), .out(Result_B[1]), .sel(Invert_B));
  Multiplexer multiplexer_15 (.in0(Data_A[0]), .in1(not_16_out), .out(Result_A[0]), .sel(Invert_A));
  not not_16 (not_16_out, Data_A[0]);
  Multiplexer multiplexer_16 (.in0(Data_B[0]), .in1(not_8_out), .out(Result_B[0]), .sel(Invert_B));
endmodule

module Instruction_Decoder (
  input  [15:0] Instruction,
  output [2:0] Reg_A,
  output [2:0] Reg_B,
  output [2:0] In_Reg,
  output [7:0] Data_In,
  output out_6,
  output out_7,
  output out_8,
  output LDI,
  output ADD_Op,
  output SUB_Op,
  output AND_Op,
  output OR_Op,
  output XOR_Op,
  output NOT_Op,
  output out_16,
  output out_17,
  output out_18,
  output out_19,
  output Halt
);

  wire or_1_out;
  wire [0:0] controlled_buffer_2_out;
  wire [5:0] controlled_buffer_1_out;
  wire [8:0] controlled_buffer_3_out;

  Decoder #(.select(4)) decoder_1 (
    .out1(out_6), .out2(out_7), .out3(out_8), .out4(LDI), .out5(ADD_Op), .out6(SUB_Op), .out7(AND_Op),
    .out8(OR_Op), .out9(XOR_Op), .out10(NOT_Op), .out11(out_16), .out12(out_17), .out13(out_18),
    .out14(out_19), .out15(Halt), .sel(Instruction[15:12]));  // open: out0, en
  assign {Reg_A, Reg_B, controlled_buffer_1_out} = or_1_out ? Instruction[11:0] : 12'bz;  // Controlled_Buffer controlled_buffer_1
  assign {In_Reg, Data_In, controlled_buffer_2_out[0]} = LDI ? Instruction[11:0] : 12'bz;  // Controlled_Buffer controlled_buffer_2
  assign {Reg_A, controlled_buffer_3_out} = NOT_Op ? Instruction[11:0] : 12'bz;  // Controlled_Buffer controlled_buffer_3
  or or_1 (or_1_out, ADD_Op, SUB_Op, AND_Op, OR_Op, XOR_Op);
  assign In_Reg = Reg_A;  // Buffer buffer_1, 3 bits wide
  assign In_Reg = Reg_A;  // Buffer buffer_2, 3 bits wide
endmodule
